// Logisim project 2.CircuitoAcumuladorDePuntuaciones.circ as structural Verilog: 2 circuits, main circuit main
module main (
  output [2:0] D2,
  output [2:0] D1,
  output [2:0] Resultado_D2,
  output [3:0] out_4,
  output [2:0] Resultado_D1,
  output [2:0] D2_2,
  output [2:0] D1_2,
  output [2:0] Resultado_D2_2,
  output [3:0] out_9,
  output [2:0] Resultado_D1_2
);

  wire button_1_out, button_2_out, button_3_out, button_4_out, clock_1_out, clock_2_out, comparator_1_eq,
       comparator_2_eq, counter_1_carry, counter_3_carry, not_1_out, not_2_out, or_1_out, or_2_out;
  wire [1:0] counter_1_q, counter_3_q;
  wire [2:0] counter_2_q, counter_4_q;

  Clock clock_1 (.out(clock_1_out));
  Button button_1 (.out(button_1_out));
  Clock clock_2 (.out(clock_2_out));
  Button button_2 (.out(button_2_out));
  Counter #(.width(2), .max('h3)) counter_1 (
    .Q(counter_1_q), .carry(counter_1_carry), .clk(button_4_out), .clr(or_2_out));  // open: load, D, count
  Register #(.width(3)) register_1 (.D(counter_2_q), .Q(D2), .clk(button_3_out), .clr(or_1_out));  // open: en
  Counter #(.width(3), .max('h6)) counter_2 (
    .Q(counter_2_q), .clk(clock_1_out), .clr(or_1_out));  // open: load, D, count, carry
  Button button_3 (.out(button_3_out));
  Counter #(.width(2), .max('h3)) counter_3 (
    .Q(counter_3_q), .carry(counter_3_carry), .clk(button_3_out), .clr(or_1_out));  // open: load, D, count
  Register #(.width(3)) register_2 (.D(counter_4_q), .Q(D2_2), .clk(button_4_out), .clr(or_2_out));  // open: en
  Counter #(.width(3), .max('h6)) counter_4 (
    .Q(counter_4_q), .clk(clock_2_out), .clr(or_2_out));  // open: load, D, count, carry
  Button button_4 (.out(button_4_out));
  or or_1 (or_1_out, button_1_out, counter_3_carry);
  Comparator #(.width(2)) comparator_1 (.a(counter_3_q), .b(2'b10), .eq(comparator_1_eq));  // open: gt, lt
  or or_2 (or_2_out, button_2_out, counter_1_carry);
  Comparator #(.width(2)) comparator_2 (.a(counter_1_q), .b(2'b10), .eq(comparator_2_eq));  // open: gt, lt
  Register #(.width(3)) register_3 (.D(D2), .Q(D1), .clk(button_3_out), .clr(or_1_out));  // open: en
  not not_1 (not_1_out, or_1_out);
  Register #(.width(3)) register_4 (.D(D2_2), .Q(D1_2), .clk(button_4_out), .clr(or_2_out));  // open: en
  not not_2 (not_2_out, or_2_out);
  // _74198 74198_1: pin names not known; wires that end beside it: 1'b1, 1'b1, D1[0], Resultado_D1[0], D1[1], Resultado_D1[1], D1[2], Resultado_D1[2], 1'b0, comparator_1_eq, 1'b1, 1'b1, 1'b0, D2[2], Resultado_D2[2], D2[1], Resultado_D2[1], D2[0], Resultado_D2[0], not_1_out
  // _74198 74198_2: pin names not known; wires that end beside it: 1'b1, 1'b1, D1_2[0], Resultado_D1_2[0], D1_2[1], Resultado_D1_2[1], D1_2[2], Resultado_D1_2[2], 1'b0, comparator_2_eq, 1'b1, 1'b1, 1'b0, D2_2[2], Resultado_D2_2[2], D2_2[1], Resultado_D2_2[1], D2_2[0], Resultado_D2_2[0], not_2_out
  SumCompleto2N3Bits sumcompleto2n3bits_1 (
    .A3(Resultado_D2[2]), .A2(Resultado_D2[1]), .A1(Resultado_D2[0]), .B3(Resultado_D1[2]),
    .B2(Resultado_D1[1]), .B1(Resultado_D1[0]), .C4(out_4[3]), .C3(out_4[2]), .C2(out_4[1]), .C1(out_4[0]));
  SumCompleto2N3Bits sumcompleto2n3bits_2 (
    .A3(Resultado_D2_2[2]), .A2(Resultado_D2_2[1]), .A1(Resultado_D2_2[0]), .B3(Resultado_D1_2[2]),
    .B2(Resultado_D1_2[1]), .B1(Resultado_D1_2[0]), .C4(out_9[3]), .C3(out_9[2]), .C2(out_9[1]), .C1(out_9[0]));
  Hex_Digit_Display hex_digit_display_1 (.value(out_4));  // open: dp
  Hex_Digit_Display hex_digit_display_2 (.value(out_9));  // open: dp

  // Notes on the sheet:
  //   de Puntuaciones
  //   Jugador 1
  //   Reset
  //   Jugador 2
  //   Reset
  //   Circuito Acumulador
  //   Contador
  //   Contador de tiradas
  //   Contador
  //   Contador de tiradas
  //   Tirar Dado
  //   (Tiradas%3==0) => Full Reset
  //   Tiradas == 2 => Load in register
  //   Tirar Dado
  //   (Tiradas%3==0) => Full Reset
  //   Tiradas == 2 => Load in register
  //   Suma de las dos tiradas
  //   Suma de las dos tiradas
  //   Puntuacion Jugador 1
  //   Puntuacion Jugador 2
endmodule

// Sum3Bits
module SumCompleto2N3Bits (
  input  A3,
  input  A2,
  input  A1,
  input  B3,
  input  B2,
  input  B1,
  output C4,
  output C3,
  output C2,
  output C1
);

  wire and_1_out, and_2_out, and_3_out, and_4_out, and_5_out, and_6_out, and_7_out, and_8_out, and_9_out,
       and_10_out, and_11_out, and_12_out, and_13_out, and_14_out, and_15_out, and_16_out, and_17_out,
       and_18_out, and_19_out, and_20_out, and_21_out, and_22_out, and_23_out, and_24_out, and_25_out,
       and_26_out, and_27_out, and_28_out, and_29_out, and_30_out, and_31_out, not_1_out, not_2_out,
       not_3_out, not_4_out, not_5_out, not_6_out, not_7_out, not_8_out, not_9_out, not_10_out, not_11_out,
       not_12_out, not_13_out, not_14_out, not_15_out, not_16_out, not_17_out, not_18_out, not_19_out,
       not_20_out, not_21_out, not_22_out, not_23_out, not_24_out, not_25_out, not_26_out, not_27_out,
       not_28_out, not_29_out, not_30_out, not_31_out, not_32_out, not_33_out, not_34_out, not_35_out,
       not_36_out, not_37_out, not_38_out, not_39_out, not_40_out, not_41_out, not_42_out, not_43_out,
       not_44_out, not_45_out, not_46_out, not_47_out, not_48_out;

  and and_1 (and_1_out, A1, B3, B2, B1);
  and and_2 (and_2_out, A2, B3, B2);
  and and_3 (and_3_out, A2, A1, B3, B1);
  and and_4 (and_4_out, A3, B3);
  and and_5 (and_5_out, A3, A1, B2, B1);
  and and_6 (and_6_out, A3, A2, B2);
  and and_7 (and_7_out, A3, A2, A1, B1);
  not not_1 (not_1_out, A3);
  not not_2 (not_2_out, A2);
  not not_3 (not_3_out, A1);
  not not_4 (not_4_out, A3);
  not not_5 (not_5_out, A2);
  not not_6 (not_6_out, B2);
  not not_7 (not_7_out, A3);
  not not_8 (not_8_out, A2);
  not not_9 (not_9_out, B1);
  not not_10 (not_10_out, A3);
  not not_11 (not_11_out, A1);
  not not_12 (not_12_out, B2);
  not not_13 (not_13_out, A3);
  not not_14 (not_14_out, B2);
  not not_15 (not_15_out, B1);
  not not_16 (not_16_out, A3);
  not not_17 (not_17_out, B3);
  not not_18 (not_18_out, A3);
  not not_19 (not_19_out, B3);
  not not_20 (not_20_out, A3);
  not not_21 (not_21_out, B3);
  not not_22 (not_22_out, A2);
  not not_23 (not_23_out, A1);
  not not_24 (not_24_out, B3);
  not not_25 (not_25_out, A2);
  not not_26 (not_26_out, B3);
  not not_27 (not_27_out, B2);
  not not_28 (not_28_out, A2);
  not not_29 (not_29_out, B3);
  not not_30 (not_30_out, B1);
  not not_31 (not_31_out, A1);
  not not_32 (not_32_out, B3);
  not not_33 (not_33_out, B2);
  not not_34 (not_34_out, B3);
  not not_35 (not_35_out, B2);
  not not_36 (not_36_out, B1);
  not not_37 (not_37_out, A2);
  not not_38 (not_38_out, A1);
  not not_39 (not_39_out, A2);
  not not_40 (not_40_out, B1);
  not not_41 (not_41_out, A2);
  not not_42 (not_42_out, B2);
  not not_43 (not_43_out, A1);
  not not_44 (not_44_out, B2);
  not not_45 (not_45_out, B2);
  not not_46 (not_46_out, B1);
  not not_47 (not_47_out, A1);
  not not_48 (not_48_out, B1);
  or or_1 (C4, and_1_out, and_2_out, and_3_out, and_4_out, and_5_out, and_6_out, and_7_out);
  and and_8 (and_8_out, not_1_out, not_2_out, not_3_out, B3);
  and and_9 (and_9_out, not_4_out, not_5_out, B3, not_6_out);
  and and_10 (and_10_out, not_7_out, not_8_out, B3, not_9_out);
  and and_11 (and_11_out, not_10_out, not_11_out, B3, not_12_out);
  and and_12 (and_12_out, not_13_out, B3, not_14_out, not_15_out);
  and and_13 (and_13_out, not_16_out, A1, not_17_out, B2, B1);
  and and_14 (and_14_out, not_18_out, A2, not_19_out, B2);
  and and_15 (and_15_out, not_20_out, A2, A1, not_21_out, B1);
  and and_16 (and_16_out, A3, not_22_out, not_23_out, not_24_out);
  and and_17 (and_17_out, A3, not_25_out, not_26_out, not_27_out);
  and and_18 (and_18_out, A3, not_28_out, not_29_out, not_30_out);
  and and_19 (and_19_out, A3, not_31_out, not_32_out, not_33_out);
  and and_20 (and_20_out, A3, not_34_out, not_35_out, not_36_out);
  and and_21 (and_21_out, A3, A1, B3, B2, B1);
  and and_22 (and_22_out, A3, A2, B3, B2);
  and and_23 (and_23_out, A3, A2, A1, B3, B1);
  and and_24 (and_24_out, not_37_out, not_38_out, B2);
  and and_25 (and_25_out, not_39_out, B2, not_40_out);
  and and_26 (and_26_out, not_41_out, A1, not_42_out, B1);
  and and_27 (and_27_out, A2, not_43_out, not_44_out);
  and and_28 (and_28_out, A2, not_45_out, not_46_out);
  and and_29 (and_29_out, A2, A1, B2, B1);
  and and_30 (and_30_out, not_47_out, B1);
  and and_31 (and_31_out, A1, not_48_out);
  or or_2 (C2, and_24_out, and_25_out, and_26_out, and_27_out, and_28_out, and_29_out);
  or or_3 (C1, and_30_out, and_31_out);
  or or_4 (C3, and_8_out, and_9_out, and_10_out, and_11_out, and_12_out, and_13_out, and_14_out, and_15_out, and_16_out, and_17_out, and_18_out, and_19_out, and_20_out, and_21_out, and_22_out, and_23_out);
endmodule
