// Logisim project CircuitoAcumuladorDePuntuaciones.circ as structural Verilog: 1 circuit, main circuit main
module main (
  output [3:0] out_1
);

  wire button_1_out, button_2_out, button_3_out, button_4_out, clock_1_out, clock_2_out;
  wire [3:0] counter_1_q, counter_2_q, register_1_q, register_3_q, register_4_q;

  Clock clock_1 (.out(clock_1_out));
  Button button_1 (.out(button_1_out));
  Clock clock_2 (.out(clock_2_out));
  Button button_2 (.out(button_2_out));
  Counter #(.width(4), .max('hf), .ongoal("load")) counter_1 (
    .Q(counter_1_q), .clk(clock_1_out), .clr(button_1_out));  // open: load, D, count, carry
  Counter #(.width(4), .max('hf), .ongoal("load")) counter_2 (
    .Q(counter_2_q), .clk(clock_2_out), .clr(button_2_out));  // open: load, D, count, carry
  Button button_3 (.out(button_3_out));
  Button button_4 (.out(button_4_out));
  Register #(.width(4)) register_1 (
    .D(counter_1_q), .en(button_3_out), .Q(register_1_q), .clk(button_3_out), .clr(button_1_out));
  Register #(.width(4)) register_2 (.D(register_1_q), .clk(button_3_out), .clr(button_1_out));  // open: en, Q
  Hex_Digit_Display hex_digit_display_1 (.value(register_3_q));  // open: dp
  Register #(.width(4)) register_3 (
    .D(counter_2_q), .en(button_4_out), .Q(register_3_q), .clk(button_4_out), .clr(button_2_out));
  Register #(.width(4)) register_4 (
    .D(register_3_q), .Q(register_4_q), .clk(button_4_out), .clr(button_2_out));  // open: en
  Hex_Digit_Display hex_digit_display_2 (.value(register_4_q));  // open: dp
  Hex_Digit_Display hex_digit_display_3 (.value(out_1));  // open: dp
  Adder #(.width(4)) adder_1 (.a(register_3_q), .b(register_4_q), .out(out_1));  // open: cin, cout
  // _74198 74198_1: pin names not known

  // Notes on the sheet:
  //   Jugador 1
  //   Reloj
  //   Reset
  //   Jugador 2
  //   Reloj
  //   Reset
  //   Tirar Dado
  //   Contador
  //   Tirar Dado
  //   Contador
  //   Circuito Acumulador de Puntuaciones
  //   2º Dado
  //   1º Dado
  //   Puntuacion
endmodule
