// Logisim project CircuitoAcumuladorDePuntuaciones1.circ as structural Verilog: 1 circuit, main circuit main
module main (
  input  [1:0] in_1,
  output [2:0] D2,
  output [2:0] D1,
  output [2:0] Resultado_D2,
  output [2:0] out_5
);

  wire button_1_out, button_2_out, clock_1_out, comparator_1_eq, counter_2_carry, not_1_out, or_1_out;
  wire [1:0] counter_2_q;
  wire [2:0] counter_1_q;

  Clock clock_1 (.out(clock_1_out));
  Button button_1 (.out(button_1_out));
  Register #(.width(3)) register_1 (.D(counter_1_q), .Q(D2), .clk(button_2_out), .clr(or_1_out));  // open: en
  Counter #(.width(3), .max('h6)) counter_1 (
    .Q(counter_1_q), .clk(clock_1_out), .clr(or_1_out));  // open: load, D, count, carry
  Button button_2 (.out(button_2_out));
  Counter #(.width(2), .max('h3)) counter_2 (
    .Q(counter_2_q), .carry(counter_2_carry), .clk(button_2_out), .clr(or_1_out));  // open: load, D, count
  or or_1 (or_1_out, button_1_out, counter_2_carry);
  Comparator #(.width(2)) comparator_1 (.a(counter_2_q), .b(in_1), .eq(comparator_1_eq));  // open: gt, lt
  Register #(.width(3)) register_2 (.D(D2), .Q(D1), .clk(button_2_out), .clr(or_1_out));  // open: en
  not not_1 (not_1_out, or_1_out);
  // _74198 74198_1: pin names not known; wires that end beside it: 1'b1, 1'b1, D1[0], out_5[0], D1[1], out_5[1], D1[2], out_5[2], 1'b0, comparator_1_eq, 1'b1, 1'b1, 1'b0, D2[2], Resultado_D2[0], D2[1], Resultado_D2[1], D2[0], Resultado_D2[2], not_1_out
  Adder #(.width(3)) adder_1 (.a(Resultado_D2), .b(out_5));  // open: out, cin, cout

  // Notes on the sheet:
  //   de Puntuaciones
  //   Reset
  //   Circuito Acumulador
  //   Contador
  //   Contador de tiradas
  //   Tirar Dado
  //   (Tiradas%3==0) => Full Reset
  //   Tiradas == 2 => Load in register
  //   Resultado D1
  //   Suma de las dos tiradas
  //   Puntuacion Jugador 1
endmodule
