// Logisim project CircuitoDado.circ as structural Verilog: 1 circuit, main circuit main
module main (
  output [2:0] Dado_2,
  output [2:0] Dado_1
);

  wire button_1_out, button_2_out, clock_1_out;
  wire [2:0] counter_1_q;

  Clock clock_1 (.out(clock_1_out));
  Button button_1 (.out(button_1_out));
  Button button_2 (.out(button_2_out));
  Counter #(.width(3), .max('h7), .ongoal("load")) counter_1 (
    .Q(counter_1_q), .clk(clock_1_out), .clr(button_1_out));  // open: load, D, count, carry
  Register #(.width(3)) register_1 (
    .D(counter_1_q), .en(button_2_out), .Q(Dado_2), .clk(button_2_out), .clr(button_1_out));
  Register #(.width(3)) register_2 (.D(Dado_2), .Q(Dado_1), .clk(button_2_out), .clr(button_1_out));  // open: en

  // Notes on the sheet:
  //   Contador
  //   Reloj
  //   Reset
  //   Circuito Dado
  //   Tirar Dado
  //   Registro
endmodule
