// Logisim project 3.CircuitoVisualizadorDelEstadoDelJuego.circ as structural Verilog: 3 circuits, main circuit main
module main (
  input  Empezar_Juego,
  output [2:0] D2,
  output [2:0] D1,
  output [2:0] Resultado_D2,
  output [2:0] Resultado_D1,
  output [3:0] out_6,
  output [2:0] D2_2,
  output [2:0] D1_2,
  output [2:0] Resultado_D2_2,
  output [2:0] Resultado_D1_2
);

  wire and_3_out, and_4_out, Apagado, Caso_Imposible, CLK, clock_1_out, comparator_1_eq, comparator_2_eq,
       comparator_3_eq, comparator_4_eq, comparator_5_eq, comparator_6_eq, comparator_7_eq, comparator_9_eq,
       comparator_10_eq, comparator_10_gt, comparator_10_lt, comparator_11_gt, comparator_12_eq,
       comparator_12_gt, comparator_12_lt, ContMax1, ContMax2, Dado_J1, Dado_J2, Full_Reset_out, GANADOR,
       not_1_out, not_2_out, not_3_out, not_4_out, not_5_out, not_6_out, not_7_out, or_2_out, or_4_out, RESET;
  wire [1:0] Cont1, Cont2;
  wire [2:0] adder_1_out, counter_2_q, counter_4_q;
  wire [3:0] PuntosJ1, PuntosJ2, transistor_1_out, transistor_3_out, transistor_5_out;

  Counter #(.width(2), .max('h3)) counter_1 (
    .Q(Cont2), .carry(ContMax2), .clk(Dado_J2), .clr(RESET));  // open: load, D, count
  Register #(.width(3)) register_1 (.D(counter_2_q), .Q(D2), .clk(Dado_J1), .clr(RESET));  // open: en
  Counter #(.width(3), .max('h6)) counter_2 (.Q(counter_2_q), .clk(CLK), .clr(RESET));  // open: load, D, count, carry
  Counter #(.width(2), .max('h3)) counter_3 (
    .Q(Cont1), .carry(ContMax1), .clk(Dado_J1), .clr(RESET));  // open: load, D, count
  Register #(.width(3)) register_2 (.D(counter_4_q), .Q(D2_2), .clk(Dado_J2), .clr(RESET));  // open: en
  Counter #(.width(3), .max('h6)) counter_4 (.Q(counter_4_q), .clk(CLK), .clr(RESET));  // open: load, D, count, carry
  Comparator #(.width(2)) comparator_1 (.a(Cont1), .b(2'b10), .eq(comparator_1_eq));  // open: gt, lt
  Comparator #(.width(2)) comparator_2 (.a(Cont2), .b(2'b10), .eq(comparator_2_eq));  // open: gt, lt
  Register #(.width(3)) register_3 (.D(D2), .Q(D1), .clk(Dado_J1), .clr(RESET));  // open: en
  not not_1 (not_1_out, RESET);
  Register #(.width(3)) register_4 (.D(D2_2), .Q(D1_2), .clk(Dado_J2), .clr(RESET));  // open: en
  not not_2 (not_2_out, RESET);
  // _74198 74198_1: pin names not known; wires that end beside it: 1'b1, 1'b1, D1[0], Resultado_D1[0], D1[1], Resultado_D1[1], D1[2], Resultado_D1[2], 1'b0, comparator_1_eq, 1'b1, 1'b1, 1'b0, D2[2], Resultado_D2[2], D2[1], Resultado_D2[1], D2[0], Resultado_D2[0], not_1_out
  // _74198 74198_2: pin names not known; wires that end beside it: 1'b1, 1'b1, D1_2[0], Resultado_D1_2[0], D1_2[1], Resultado_D1_2[1], D1_2[2], Resultado_D1_2[2], 1'b0, comparator_2_eq, 1'b1, 1'b1, 1'b0, D2_2[2], Resultado_D2_2[2], D2_2[1], Resultado_D2_2[1], D2_2[0], Resultado_D2_2[0], not_2_out
  not not_3 (not_3_out, Empezar_Juego);
  or or_1 (RESET, ContMax2, ContMax1, Full_Reset_out, not_3_out);
  Clock clock_1 (.out(clock_1_out));
  and and_1 (CLK, clock_1_out, Empezar_Juego);
  Button Full_Reset (.out(Full_Reset_out));
  SumCompleto2N3Bits sumcompleto2n3bits_1 (
    .A3(Resultado_D2[2]), .A2(Resultado_D2[1]), .A1(Resultado_D2[0]), .B3(Resultado_D1[2]),
    .B2(Resultado_D1[1]), .B1(Resultado_D1[0]), .C4(PuntosJ1[3]), .C3(PuntosJ1[2]), .C2(PuntosJ1[1]),
    .C1(PuntosJ1[0]));
  Adder #(.width(3)) adder_1 (.a({1'b0, Cont1}), .b({1'b0, Cont2}), .out(adder_1_out));  // open: cin, cout
  SumCompleto2N3Bits sumcompleto2n3bits_2 (
    .A3(Resultado_D2_2[2]), .A2(Resultado_D2_2[1]), .A1(Resultado_D2_2[0]), .B3(Resultado_D1_2[2]),
    .B2(Resultado_D1_2[1]), .B1(Resultado_D1_2[0]), .C4(PuntosJ2[3]), .C3(PuntosJ2[2]), .C2(PuntosJ2[1]),
    .C1(PuntosJ2[0]));
  Hex_Digit_Display hex_digit_display_1 (.value(PuntosJ1));  // open: dp
  // Probe on PuntosJ1
  Button J1__A (.out(Dado_J1));
  Comparator #(.width(3), .mode("unsigned")) comparator_3 (
    .a(adder_1_out), .b(3'b000), .eq(comparator_3_eq));  // open: gt, lt
  Hex_Digit_Display hex_digit_display_2 (.value(PuntosJ2));  // open: dp
  // Probe on PuntosJ2
  Button J2__b (.out(Dado_J2));
  CircEstadoJuego circestadojuego_1 (
    .OnOff(Empezar_Juego), .SumCont0(comparator_3_eq), .Pts0(or_2_out), .E0(out_6[3]), .E1(out_6[2]),
    .E2(out_6[1]), .E3(out_6[0]));
  Comparator #(.width(3), .mode("unsigned")) comparator_4 (
    .a(3'b100), .b(adder_1_out), .eq(comparator_4_eq));  // open: gt, lt
  Hex_Digit_Display hex_digit_display_3 (.value(out_6));  // open: dp
  or or_2 (or_2_out, comparator_5_eq, comparator_6_eq);
  Comparator #(.width(4), .mode("unsigned")) comparator_5 (
    .a(PuntosJ1), .b(4'b0000), .eq(comparator_5_eq));  // open: gt, lt
  Comparator #(.width(4), .mode("unsigned")) comparator_6 (
    .a(PuntosJ2), .b(4'b0000), .eq(comparator_6_eq));  // open: gt, lt
  and and_2 (Caso_Imposible, comparator_4_eq, comparator_5_eq, comparator_6_eq);
  Comparator #(.width(4)) comparator_7 (.a(4'b0010), .b(out_6), .eq(comparator_7_eq));  // open: gt, lt
  or or_3 (GANADOR, comparator_7_eq, Caso_Imposible);
  Comparator #(.width(4)) comparator_8 (.a(4'b0000), .b(out_6), .eq(Apagado));  // open: gt, lt
  Transistor #(.\type ("n"), .width(4)) transistor_1 (.in(out_6), .out(transistor_1_out), .gate(Apagado));
  Comparator #(.width(4)) comparator_9 (.a(out_6), .b(4'b1101), .eq(comparator_9_eq));  // open: gt, lt
  Transistor #(.\type ("n"), .width(4)) transistor_2 (.in(out_6), .out(transistor_1_out), .gate(comparator_9_eq));
  Comparator #(.width(4)) comparator_10 (
    .a({1'b0, D2}), .b({1'b0, D2_2}), .gt(comparator_10_gt), .eq(comparator_10_eq), .lt(comparator_10_lt));
  or or_4 (or_4_out, comparator_10_lt, comparator_10_eq, and_3_out);
  not not_4 (not_4_out, Apagado);
  not not_5 (not_5_out, comparator_9_eq);
  Transistor #(.\type ("n"), .width(4)) transistor_3 (.in({1'b0, D2}), .out(transistor_3_out), .gate(comparator_10_gt));
  Transistor #(.\type ("n"), .width(4)) transistor_4 (.in({1'b0, D2_2}), .out(transistor_3_out), .gate(or_4_out));
  and and_3 (and_3_out, comparator_10_eq, comparator_11_gt);
  Comparator #(.width(4)) comparator_11 (.a({1'b0, D2_2}), .b(4'b0000), .gt(comparator_11_gt));  // open: eq, lt
  Comparator #(.width(4), .mode("unsigned")) comparator_12 (
    .a(PuntosJ1), .b(PuntosJ2), .gt(comparator_12_gt), .eq(comparator_12_eq), .lt(comparator_12_lt));
  Transistor #(.\type ("n"), .width(4)) transistor_5 (.in(4'b1010), .out(transistor_5_out), .gate(comparator_12_gt));
  Transistor #(.\type ("n"), .width(4)) transistor_6 (.in(transistor_5_out), .out(transistor_1_out), .gate(GANADOR));
  Hex_Digit_Display hex_digit_display_4 (.value(transistor_1_out));  // open: dp
  not not_6 (not_6_out, GANADOR);
  not not_7 (not_7_out, Caso_Imposible);
  and and_4 (and_4_out, not_5_out, not_4_out, not_6_out, not_7_out);
  Transistor #(.\type ("n"), .width(4)) transistor_7 (.in(transistor_3_out), .out(transistor_1_out), .gate(and_4_out));
  Transistor #(.\type ("n"), .width(4)) transistor_8 (.in(4'b1011), .out(transistor_5_out), .gate(comparator_12_lt));
  Transistor #(.\type ("n"), .width(4)) transistor_9 (.in(4'b1110), .out(transistor_5_out), .gate(comparator_12_eq));

  // Other names for the same wires on the sheet: Ult__J1[2:0] = D2; Ult__J2[2:0] = D2_2

  // Notes on the sheet:
  //   Jugador 1 (A)
  //   Jugador 2 (b)
  //   Contador
  //   (Tiradas%3==0) => Full Reset
  //   Contador de tiradas
  //   Contador
  //   (Tiradas%3==0) => Full Reset
  //   Contador de tiradas
  //   Tiradas == 2 => Load in register
  //   Tiradas == 2 => Load in register
  //   Ultima tirada Jugador 1
  //   0 => Apagado
  //   1 => Dado funcionando
  //   Ultima tirada Jugador 2
  //   Suma de las dos tiradas
  //   Suma de las dos tiradas
  //   Puntuacion Jugador 1
  //   Puntuacion Jugador 2
  //   Tirar Dados
  //   del Estado del Juego
  //   Sub-Circuito ESTADO
  //   Circuito Visualizador
  //   PREVIO
  //   ESTADO
  //   DEL
  //   JUEGO
  //   Comparador de puntuaciones
  //   (Sin signo) ¿Quien gana?
  //   ¿Hay ganador?
  //   ¿Esta apagado?
  //   ¿Corriendo el dado?
  //   J1
  //   J2
  //   Empate
  //   ESTADO
  //   DEL
  //   JUEGO
endmodule

// Sum3Bits
module SumCompleto2N3Bits (
  input  A3,
  input  A2,
  input  A1,
  input  B3,
  input  B2,
  input  B1,
  output C4,
  output C3,
  output C2,
  output C1
);

  wire and_1_out, and_2_out, and_3_out, and_4_out, and_5_out, and_6_out, and_7_out, and_8_out, and_9_out,
       and_10_out, and_11_out, and_12_out, and_13_out, and_14_out, and_15_out, and_16_out, and_17_out,
       and_18_out, and_19_out, and_20_out, and_21_out, and_22_out, and_23_out, and_24_out, and_25_out,
       and_26_out, and_27_out, and_28_out, and_29_out, and_30_out, and_31_out, not_1_out, not_2_out,
       not_3_out, not_4_out, not_5_out, not_6_out, not_7_out, not_8_out, not_9_out, not_10_out, not_11_out,
       not_12_out, not_13_out, not_14_out, not_15_out, not_16_out, not_17_out, not_18_out, not_19_out,
       not_20_out, not_21_out, not_22_out, not_23_out, not_24_out, not_25_out, not_26_out, not_27_out,
       not_28_out, not_29_out, not_30_out, not_31_out, not_32_out, not_33_out, not_34_out, not_35_out,
       not_36_out, not_37_out, not_38_out, not_39_out, not_40_out, not_41_out, not_42_out, not_43_out,
       not_44_out, not_45_out, not_46_out, not_47_out, not_48_out;

  and and_1 (and_1_out, A1, B3, B2, B1);
  and and_2 (and_2_out, A2, B3, B2);
  and and_3 (and_3_out, A2, A1, B3, B1);
  and and_4 (and_4_out, A3, B3);
  and and_5 (and_5_out, A3, A1, B2, B1);
  and and_6 (and_6_out, A3, A2, B2);
  and and_7 (and_7_out, A3, A2, A1, B1);
  not not_1 (not_1_out, A3);
  not not_2 (not_2_out, A2);
  not not_3 (not_3_out, A1);
  not not_4 (not_4_out, A3);
  not not_5 (not_5_out, A2);
  not not_6 (not_6_out, B2);
  not not_7 (not_7_out, A3);
  not not_8 (not_8_out, A2);
  not not_9 (not_9_out, B1);
  not not_10 (not_10_out, A3);
  not not_11 (not_11_out, A1);
  not not_12 (not_12_out, B2);
  not not_13 (not_13_out, A3);
  not not_14 (not_14_out, B2);
  not not_15 (not_15_out, B1);
  not not_16 (not_16_out, A3);
  not not_17 (not_17_out, B3);
  not not_18 (not_18_out, A3);
  not not_19 (not_19_out, B3);
  not not_20 (not_20_out, A3);
  not not_21 (not_21_out, B3);
  not not_22 (not_22_out, A2);
  not not_23 (not_23_out, A1);
  not not_24 (not_24_out, B3);
  not not_25 (not_25_out, A2);
  not not_26 (not_26_out, B3);
  not not_27 (not_27_out, B2);
  not not_28 (not_28_out, A2);
  not not_29 (not_29_out, B3);
  not not_30 (not_30_out, B1);
  not not_31 (not_31_out, A1);
  not not_32 (not_32_out, B3);
  not not_33 (not_33_out, B2);
  not not_34 (not_34_out, B3);
  not not_35 (not_35_out, B2);
  not not_36 (not_36_out, B1);
  not not_37 (not_37_out, A2);
  not not_38 (not_38_out, A1);
  not not_39 (not_39_out, A2);
  not not_40 (not_40_out, B1);
  not not_41 (not_41_out, A2);
  not not_42 (not_42_out, B2);
  not not_43 (not_43_out, A1);
  not not_44 (not_44_out, B2);
  not not_45 (not_45_out, B2);
  not not_46 (not_46_out, B1);
  not not_47 (not_47_out, A1);
  not not_48 (not_48_out, B1);
  or or_1 (C4, and_1_out, and_2_out, and_3_out, and_4_out, and_5_out, and_6_out, and_7_out);
  and and_8 (and_8_out, not_1_out, not_2_out, not_3_out, B3);
  and and_9 (and_9_out, not_4_out, not_5_out, B3, not_6_out);
  and and_10 (and_10_out, not_7_out, not_8_out, B3, not_9_out);
  and and_11 (and_11_out, not_10_out, not_11_out, B3, not_12_out);
  and and_12 (and_12_out, not_13_out, B3, not_14_out, not_15_out);
  and and_13 (and_13_out, not_16_out, A1, not_17_out, B2, B1);
  and and_14 (and_14_out, not_18_out, A2, not_19_out, B2);
  and and_15 (and_15_out, not_20_out, A2, A1, not_21_out, B1);
  and and_16 (and_16_out, A3, not_22_out, not_23_out, not_24_out);
  and and_17 (and_17_out, A3, not_25_out, not_26_out, not_27_out);
  and and_18 (and_18_out, A3, not_28_out, not_29_out, not_30_out);
  and and_19 (and_19_out, A3, not_31_out, not_32_out, not_33_out);
  and and_20 (and_20_out, A3, not_34_out, not_35_out, not_36_out);
  and and_21 (and_21_out, A3, A1, B3, B2, B1);
  and and_22 (and_22_out, A3, A2, B3, B2);
  and and_23 (and_23_out, A3, A2, A1, B3, B1);
  and and_24 (and_24_out, not_37_out, not_38_out, B2);
  and and_25 (and_25_out, not_39_out, B2, not_40_out);
  and and_26 (and_26_out, not_41_out, A1, not_42_out, B1);
  and and_27 (and_27_out, A2, not_43_out, not_44_out);
  and and_28 (and_28_out, A2, not_45_out, not_46_out);
  and and_29 (and_29_out, A2, A1, B2, B1);
  and and_30 (and_30_out, not_47_out, B1);
  and and_31 (and_31_out, A1, not_48_out);
  or or_2 (C2, and_24_out, and_25_out, and_26_out, and_27_out, and_28_out, and_29_out);
  or or_3 (C1, and_30_out, and_31_out);
  or or_4 (C3, and_8_out, and_9_out, and_10_out, and_11_out, and_12_out, and_13_out, and_14_out, and_15_out, and_16_out, and_17_out, and_18_out, and_19_out, and_20_out, and_21_out, and_22_out, and_23_out);
endmodule

// ESTADO
module CircEstadoJuego (
  input  OnOff,
  input  SumCont0,
  input  Pts0,
  output E0,
  output E1,
  output E2,
  output E3
);

  wire not_1_out;

  and and_1 (E0, OnOff, SumCont0, Pts0);
  and and_2 (E1, OnOff, SumCont0, Pts0);
  not not_1 (not_1_out, Pts0);
  and and_3 (E3, OnOff, Pts0);
  and and_4 (E2, OnOff, not_1_out);
endmodule
