// Logisim project CircuitoDadoConRegistro74198.circ as structural Verilog: 1 circuit, main circuit main
module main (
  input  in_1
);

  wire button_1_out, button_2_out, clock_1_out;
  wire [3:0] counter_1_q, register_1_q, register_2_q;

  Clock clock_1 (.out(clock_1_out));
  Button button_1 (.out(button_1_out));
  Button button_2 (.out(button_2_out));
  Counter #(.width(4), .max('hf), .ongoal("load")) counter_1 (
    .Q(counter_1_q), .clk(clock_1_out), .clr(button_1_out));  // open: load, D, count, carry
  Register #(.width(4)) register_1 (
    .D(counter_1_q), .en(button_2_out), .Q(register_1_q), .clk(button_2_out), .clr(button_1_out));
  Hex_Digit_Display hex_digit_display_1 (.value(register_1_q));  // open: dp
  Hex_Digit_Display hex_digit_display_2 (.value(register_2_q));  // open: dp
  Register #(.width(4)) register_2 (
    .D(register_1_q), .Q(register_2_q), .clk(button_2_out), .clr(button_1_out));  // open: en
  Comparator comparator_1 ();  // open: a, b, gt, eq, lt
  // _74198 74198_1: pin names not known; wires that end beside it: in_1, in_1, 1'b0, 1'b1

  // Notes on the sheet:
  //   Circuito Dado con Registro 74198
  //   Contador
  //   Reloj
  //   Reset
  //   Tirar Dado
  //   Registro
  //   Dado 1
  //   Dado 2
  //   Registro
endmodule
