// Logisim project DadoDigital.circ as structural Verilog: 1 circuit, main circuit main
module main (
  input  in_1,
  input  Reset,
  input  in_3
);

  wire clock_1_out, clock_2_out, j_k_ff_1_q, j_k_ff_1_qn, j_k_ff_2_q, j_k_ff_2_qn, j_k_ff_3_q, j_k_ff_3_qn,
       j_k_ff_4_q, undriven;
  wire [7:0] counter_1_q;

  Clock clock_1 (.out(clock_1_out));
  Clock clock_2 (.out(clock_2_out));
  J_K_Flip_Flop j_k_ff_1 (
    .J(in_1), .clk(undriven), .K(in_1), .Q(j_k_ff_1_q), .Qn(j_k_ff_1_qn), .en(in_1));  // open: preset, reset
  Counter counter_1 (.Q(counter_1_q), .clk(clock_2_out), .clr(Reset));  // open: load, D, count, carry
  J_K_Flip_Flop j_k_ff_2 (
    .J(in_1), .clk(j_k_ff_1_qn), .K(in_1), .Q(j_k_ff_2_q), .Qn(j_k_ff_2_qn), .en(in_1));  // open: preset, reset
  Counter counter_2 (.D(counter_1_q), .clk(in_3));  // open: load, count, Q, carry, clr
  J_K_Flip_Flop j_k_ff_3 (
    .J(in_1), .clk(j_k_ff_2_qn), .K(in_1), .Q(j_k_ff_3_q), .Qn(j_k_ff_3_qn), .en(in_1));  // open: preset, reset
  J_K_Flip_Flop j_k_ff_4 (.J(in_1), .clk(j_k_ff_3_qn), .K(in_1), .Q(j_k_ff_4_q), .en(in_1));  // open: Qn, preset, reset

  // Notes on the sheet:
  //   RELOJ
  //   Contador
  //   DADO
  //   OPCION 1 (MAL)
  //   OPCION 2
  //   Resultado
endmodule
