// Logisim project DadoDigitalConRegistro74198.circ as structural Verilog: 1 circuit, main circuit main
module main (
  input  in_1,
  input  in_2,
  output [3:0] D2,
  output [3:0] D1,
  output [3:0] Resultado_D2,
  output [3:0] out_6
);

  wire button_1_out, button_2_out, clock_1_out, n74198_1_p11, not_1_out;
  wire [3:0] counter_1_q;

  Button button_1 (.out(button_1_out));
  Clock clock_1 (.out(clock_1_out));
  not not_1 (not_1_out, button_1_out);
  Register #(.width(4)) register_1 (.D(counter_1_q), .Q(D2), .clk(button_2_out), .clr(button_1_out));  // open: en
  Counter #(.width(4), .max('hf)) counter_1 (
    .Q(counter_1_q), .clk(clock_1_out), .clr(button_1_out));  // open: load, D, count, carry
  Button button_2 (.out(button_2_out));
  Register #(.width(4)) register_2 (.D(D2), .Q(D1), .clk(button_2_out), .clr(button_1_out));  // open: en
  // _74198 74198_1: pin names not known; wires that end beside it: in_1, in_1, D1[0], out_6[0], D1[1], out_6[1], D1[2], out_6[2], D1[3], out_6[3], n74198_1_p11, in_2, in_2, D2[3], Resultado_D2[3], D2[2], Resultado_D2[2], D2[1], Resultado_D2[1], D2[0], Resultado_D2[0], not_1_out
  Button button_3 (.out(n74198_1_p11));

  // Notes on the sheet:
  //   Reset
  //   OPCION 2
  //   Contador
  //   Tirar Dado
  //   Resultado D1
  //   Al tirar dos veces ejecutar Load
  //   Load
endmodule
