// Logisim project Puertas Logicas.circ as structural Verilog: 1 circuit, main circuit main
module main (
  input  SI,
  input  NOT,
  input  in_3,
  input  NAND,
  input  in_5,
  input  in_6,
  input  OR,
  input  NOR,
  input  in_9,
  input  in_10,
  input  in_11,
  input  XNOR,
  input  in_13,
  input  in_14,
  output out_15,
  output out_16,
  output out_17,
  output out_18,
  output out_19,
  output out_20,
  output out_21,
  output out_22
);

  and and_1 (out_17, in_3, in_5);
  or or_1 (out_19, OR, in_9);
  xor xor_1 (out_21, in_11, in_13);
  not not_1 (out_16, NOT);
  nand nand_1 (out_18, NAND, in_6);
  nor nor_1 (out_20, NOR, in_10);
  xnor xnor_1 (out_22, XNOR, in_14);

  assign out_15 = SI;

  // Notes on the sheet:
  //   AND
  //   XOR (OR exclusiva)
  //   Puertas Lógicas
endmodule
