// Logisim project Registro74198(1).circ as structural Verilog: 1 circuit, main circuit main
module main (
  input  in_1,
  input  Register,
  input  in_3,
  input  in_4,
  output [3:0] Counter,
  output [3:0] out_6
);

  wire button_1_out, button_2_out, clock_1_out, n74198_1_p16;

  Hex_Digit_Display hex_digit_display_1 (.value(Counter));  // open: dp
  Button button_1 (.out(button_1_out));
  Clock clock_1 (.out(clock_1_out));
  Counter #(.width(4), .max('hf)) counter_1 (
    .Q(Counter), .clk(clock_1_out), .clr(button_1_out));  // open: load, D, count, carry
  // _74198 74198_1: pin names not known; wires that end beside it: Register, in_1, Counter[3], out_6[0], Counter[2], out_6[1], Counter[1], out_6[2], Counter[0], out_6[3], clock_1_out, 1'b0, 1'b1, in_3, in_4, n74198_1_p16
  not not_1 (n74198_1_p16, button_2_out);
  Button button_2 (.out(button_2_out));
  Hex_Digit_Display hex_digit_display_2 (.value(out_6));  // open: dp

  // Notes on the sheet:
  //   Reset
  //   Reset
endmodule
