// Logisim project Registro74198.circ as structural Verilog: 1 circuit, main circuit main
module main (
  input  in_1,
  input  Register,
  input  in_3,
  input  in_4,
  input  in_5,
  input  in_6,
  input  in_7,
  input  in_8,
  output out_9,
  output out_10,
  output out_11,
  output out_12,
  output out_13,
  output out_14,
  output out_15,
  output out_16,
  output [3:0] out_17
);

  wire button_1_out, button_2_out, clock_1_out, clock_2_out, n74198_1_p14;
  wire [3:0] counter_1_q;

  Button button_1 (.out(button_1_out));
  Clock clock_1 (.out(clock_1_out));
  Counter #(.width(4), .max('hf)) counter_1 (
    .Q(counter_1_q), .clk(clock_1_out), .clr(button_1_out));  // open: load, D, count, carry
  // _74198 74198_1: pin names not known; wires that end beside it: Register, in_1, counter_1_q[0], out_17[3], counter_1_q[1], out_17[2], counter_1_q[2], out_17[1], counter_1_q[3], out_17[0], clock_1_out, 1'b0, 1'b1, n74198_1_p14, in_3
  Button button_2 (.out(button_2_out));
  not not_1 (n74198_1_p14, button_2_out);
  Clock clock_2 (.out(clock_2_out));
  // _74198 74198_2: pin names not known; wires that end beside it: in_5, in_4, in_7, out_9, out_11, out_13, out_15, clock_2_out, 1'b0, 1'b1, in_6, out_10, out_12, out_14, out_16, in_8

  // Notes on the sheet:
  //   Reset
  //   Counter
  //   Reset
endmodule
