// Logisim project Ekaitz_Arriola_Rodrigo_Lopez_Gonzalo_Fernandez.circ as structural Verilog: 6 circuits, main circuit 4Bit_ALU
module _4Bit_ALU (
  input  CLOCK,
  input  A_A,
  input  B_A,
  input  C_A,
  input  D_A,
  input  A_B,
  input  B_B,
  input  C_B,
  input  D_B,
  input  A_MUX,
  input  B_MUX,
  input  ON_OFF,
  input  _5__Vcc,
  input  _12__GND,
  input  CARRY_IN,
  input  Shifter_In,
  output OVERFLOW,
  output D_C,
  output C_C,
  output B_C,
  output A_C,
  output CARRY_OUT,
  output Shifter_Out
);

  wire and_1_out, n7483fixed_1__14__cout, n7483fixed_2__14__cout, not_1_out, not_2_out, not_3_out,
       shift_register_3_q0, shift_register_3_q1, shift_register_3_q2, shift_register_3_q3, t_ff_1_qn;
  wire [3:0] n7408_1_p9, n7483fixed_1__9__s1, n7483fixed_2__9__s1, not_4_out,
       registro_de_desplazamiento_1_ultimo__3, shift_register_1_q0, shift_register_2_q0;

  not not_1 (not_1_out, 1'b0);
  Shift_Register #(.length(4)) shift_register_1 (
    .shift(1'b0), .clk(CLOCK), .load(not_1_out), .d0(A_A), .q0(shift_register_1_q0[0]), .d1(B_A),
    .q1(shift_register_1_q0[1]), .d2(C_A), .q2(shift_register_1_q0[2]), .d3(D_A), .q3(shift_register_1_q0[3]));  // open: in, out, clr
  not not_2 (not_2_out, 1'b0);
  Shift_Register #(.length(4)) shift_register_2 (
    .shift(1'b0), .clk(CLOCK), .load(not_2_out), .d0(A_B), .q0(shift_register_2_q0[0]), .d1(B_B),
    .q1(shift_register_2_q0[1]), .d2(C_B), .q2(shift_register_2_q0[2]), .d3(D_B), .q3(shift_register_2_q0[3]));  // open: in, out, clr
  T_Flip_Flop t_ff_1 (.clk(CLOCK), .T(CLOCK), .Qn(t_ff_1_qn));  // open: Q, preset, reset, en
  Shift_Register #(.length(4)) shift_register_3 (
    .in(Shifter_In), .clk(CLOCK), .out(Shifter_Out), .load(t_ff_1_qn), .d0(shift_register_1_q0[0]),
    .q0(shift_register_3_q0), .d1(shift_register_1_q0[1]), .q1(shift_register_3_q1),
    .d2(shift_register_1_q0[2]), .q2(shift_register_3_q2), .d3(shift_register_1_q0[3]),
    .q3(shift_register_3_q3));  // open: shift, clr
  not not_3 (not_3_out, CLOCK);
  assign not_4_out = ~shift_register_2_q0;  // NOT_Gate not_4, 4 bits wide
  and and_1 (and_1_out, t_ff_1_qn, not_3_out);
  registro_de_desplazamiento registro_de_desplazamiento_1 (
    .D(shift_register_3_q0), .C(shift_register_3_q1), .B(shift_register_3_q2), .A(shift_register_3_q3),
    .ENABLE(and_1_out), .Primero__0(registro_de_desplazamiento_1_ultimo__3[3]),
    ._1(registro_de_desplazamiento_1_ultimo__3[2]), ._2(registro_de_desplazamiento_1_ultimo__3[1]),
    .Ultimo__3(registro_de_desplazamiento_1_ultimo__3[0]));
  // _7408 7408_1: pin names not known; wires that end beside it: 1'b0, n7408_1_p9[2], n7408_1_p9[1], shift_register_1_q0[1], shift_register_2_q0[2], shift_register_2_q0[1], shift_register_1_q0[2], n7408_1_p9[3], n7408_1_p9[0], shift_register_1_q0[0], shift_register_2_q0[3], shift_register_2_q0[0], shift_register_1_q0[3], 1'b1
  _7483fixed u_7483fixed_1 (
    ._1__A4(shift_register_1_q0[0]), ._2__S3(n7483fixed_1__9__s1[2]), ._3__A3(shift_register_1_q0[1]),
    ._4__B3(shift_register_2_q0[1]), ._5__Vcc(1'b1), ._6__S2(n7483fixed_1__9__s1[1]),
    ._7__B2(shift_register_2_q0[2]), ._8__A2(shift_register_1_q0[2]), ._16__B4(shift_register_2_q0[0]),
    ._15__S4(n7483fixed_1__9__s1[3]), ._14__Cout(n7483fixed_1__14__cout), ._13__Cin(CARRY_IN),
    ._12__GND(1'b0), ._11__B1(shift_register_2_q0[3]), ._10__A1(shift_register_1_q0[3]),
    ._9__S1(n7483fixed_1__9__s1[0]));
  _7483fixed u_7483fixed_2 (
    ._1__A4(shift_register_1_q0[0]), ._2__S3(n7483fixed_2__9__s1[2]), ._3__A3(shift_register_1_q0[1]),
    ._4__B3(not_4_out[1]), ._5__Vcc(1'b1), ._6__S2(n7483fixed_2__9__s1[1]), ._7__B2(not_4_out[2]),
    ._8__A2(shift_register_1_q0[2]), ._16__B4(not_4_out[0]), ._15__S4(n7483fixed_2__9__s1[3]),
    ._14__Cout(n7483fixed_2__14__cout), ._13__Cin(1'b1), ._12__GND(1'b0), ._11__B1(not_4_out[3]),
    ._10__A1(shift_register_1_q0[3]), ._9__S1(n7483fixed_2__9__s1[0]));
  // Probe on registro_de_desplazamiento_1_ultimo__3
  // Probe on n7408_1_p9
  // Probe on n7483fixed_1__9__s1
  // Probe on n7483fixed_1__14__cout
  // Probe on n7483fixed_2__9__s1
  // Probe on n7483fixed_2__14__cout
  Multiplexer #(.select(2), .width(4), .disabled(0)) multiplexer_1 (
    .in0(n7408_1_p9), .in1(n7483fixed_1__9__s1), .in2(n7483fixed_2__9__s1),
    .in3(registro_de_desplazamiento_1_ultimo__3), .out({A_C, B_C, C_C, D_C}), .sel({B_MUX, A_MUX}),
    .en(ON_OFF));
  overflow overflow_1 (
    .Bit_DelA(shift_register_1_q0[0]), .Bit_DelB(shift_register_2_q0[0]), .Bit_DelC(A_C), .A_MUX(A_MUX),
    .B_MUX(B_MUX), .overflow(OVERFLOW));
  acarreo acarreo_1 (.A(A_MUX), .B(B_MUX), .S(n7483fixed_1__14__cout), .R(n7483fixed_2__14__cout), .carry(CARRY_OUT));
  LED led_1 (.in(OVERFLOW));
  LED led_2 (.in(CARRY_OUT));

  // Notes on the sheet:
  //   ALU
  //   ORDEN:
  //   A B C D
  //   Se supone que hay que introducir si o si un 0, pero hemos puesto
  //   Para la suma/resta usamos el 7483 en vez del 74283
  //   Pero habia una errata en dicho chip, por eso hicimos una edicion reparandolo
  //   Usamos tambien un circuito para el overflow y otro para el carry
  //   estos dos pines para poder encadenar este circuito en serie
  //   GND(7408)
  //   Vcc(7408)
  //   GND(7483[0]))
  //   GND(7483[1]))
  //   Vcc(7483[0])
  //   Vcc(7483[1])
  //   CARRY IN (+1 del Ca2)
  //   AMux) = 1 y B(Mux) = 0 -->  Suma
  //   A(Mux) = 0 y  B(Mux) = 1 --> Resta
  //   A(Mux) = 1 y B(Mux) = 1  --> A>>0
  //   A(Mux) = 0 y B(Mux) = 0  --> &
endmodule

// 7483
module _7483fixed (
  input  _1__A4,
  input  _16__B4,
  input  _3__A3,
  input  _4__B3,
  input  _13__Cin,
  input  _5__Vcc,
  input  _12__GND,
  input  _11__B1,
  input  _7__B2,
  input  _10__A1,
  input  _8__A2,
  output _2__S3,
  output _15__S4,
  output _14__Cout,
  output _6__S2,
  output _9__S1
);

  wire and_1_out, and_2_out, and_3_out, and_4_out, and_5_out, and_6_out, and_7_out, and_8_out, and_9_out,
       and_10_out, and_11_out, and_12_out, and_13_out, and_14_out, nand_1_out, nand_2_out, nand_3_out,
       nand_4_out, nor_1_out, nor_2_out, nor_3_out, nor_4_out, nor_6_out, nor_7_out, nor_8_out, not_1_out,
       not_2_out, not_3_out, not_4_out, not_5_out, not_6_out;

  nand nand_1 (nand_1_out, _16__B4, _1__A4);
  nor nor_1 (nor_1_out, _16__B4, _1__A4);
  nand nand_2 (nand_2_out, _4__B3, _3__A3);
  nor nor_2 (nor_2_out, _4__B3, _3__A3);
  nand nand_3 (nand_3_out, _7__B2, _8__A2);
  nor nor_3 (nor_3_out, _7__B2, _8__A2);
  nand nand_4 (nand_4_out, _11__B1, _10__A1);
  nor nor_4 (nor_4_out, _11__B1, _10__A1);
  and and_1 (and_1_out, nor_2_out, nand_1_out);
  and and_2 (and_2_out, nor_3_out, nand_1_out, nand_2_out);
  and and_3 (and_3_out, nor_4_out, nand_1_out, nand_2_out, nand_3_out);
  and and_4 (and_4_out, nand_1_out, nand_2_out, nand_3_out, nand_4_out, not_2_out);
  not not_1 (not_1_out, nor_1_out);
  and and_5 (and_5_out, nor_3_out, nand_2_out);
  and and_6 (and_6_out, nor_4_out, nand_2_out, nand_3_out);
  and and_7 (and_7_out, nand_2_out, nand_3_out, nand_4_out, not_2_out);
  not not_2 (not_2_out, _13__Cin);
  not not_3 (not_3_out, nor_2_out);
  and and_8 (and_8_out, nor_4_out, nand_3_out);
  and and_9 (and_9_out, nand_3_out, nand_4_out, not_2_out);
  not not_4 (not_4_out, nor_3_out);
  and and_10 (and_10_out, nand_4_out, not_2_out);
  not not_5 (not_5_out, nor_4_out);
  not not_6 (not_6_out, not_2_out);
  nor nor_5 (_14__Cout, nor_1_out, and_1_out, and_2_out, and_3_out, and_4_out);
  and and_11 (and_11_out, nand_1_out, not_1_out);
  and and_12 (and_12_out, nand_2_out, not_3_out);
  and and_13 (and_13_out, nand_3_out, not_4_out);
  and and_14 (and_14_out, nand_4_out, not_5_out);
  xor xor_1 (_15__S4, and_11_out, nor_6_out);
  nor nor_6 (nor_6_out, nor_2_out, and_5_out, and_6_out, and_7_out);
  xor xor_2 (_2__S3, and_12_out, nor_7_out);
  nor nor_7 (nor_7_out, nor_3_out, and_8_out, and_9_out);
  xor xor_3 (_6__S2, and_13_out, nor_8_out);
  nor nor_8 (nor_8_out, nor_4_out, and_10_out);
  xor xor_4 (_9__S1, and_14_out, not_6_out);

  // Notes on the sheet:
  //   7483: 4-bit full fixed adder
endmodule

// OV
module overflow (
  input  Bit_DelA,
  input  Bit_DelB,
  input  Bit_DelC,
  input  A_MUX,
  input  B_MUX,
  output overflow
);

  wire and_1_out, and_2_out, and_3_out, not_1_out, not_2_out, not_3_out, or_1_out, xnor_1_out, xor_1_out,
       xor_2_out;

  not not_1 (not_1_out, A_MUX);
  and and_1 (and_1_out, not_1_out, B_MUX);
  not not_2 (not_2_out, Bit_DelB);
  not not_3 (not_3_out, and_1_out);
  and and_2 (and_2_out, not_2_out, and_1_out);
  or or_1 (or_1_out, and_2_out, and_3_out);
  and and_3 (and_3_out, Bit_DelB, not_3_out);
  xnor xnor_1 (xnor_1_out, Bit_DelA, or_1_out);
  xor xor_1 (xor_1_out, or_1_out, Bit_DelC);
  xor xor_2 (xor_2_out, A_MUX, B_MUX);
  and and_4 (overflow, xnor_1_out, xor_1_out, xor_2_out);

  // Notes on the sheet:
  //   Overflow
  //   Cuando es resta, devuelve !B
  //   Cuando no, devuelve B
endmodule

// CARRY
module acarreo (
  input  A,
  input  B,
  input  S,
  input  R,
  output carry
);

  wire and_1_out, and_2_out, not_1_out, not_2_out;

  not not_1 (not_1_out, A);
  not not_2 (not_2_out, B);
  and and_1 (and_1_out, not_1_out, B, R);
  or or_1 (carry, and_1_out, and_2_out);
  and and_2 (and_2_out, A, not_2_out, S);

  // Notes on the sheet:
  //   Acarreo
endmodule

// SHIFT REGISTER
module registro_de_desplazamiento (
  input  D,
  input  C,
  input  B,
  input  A,
  input  ENABLE,
  output Primero__0,
  output _1,
  output _2,
  output Ultimo__3
);

  Register #(.width(1), .trigger("high")) register_1 (.D(D), .Q(Primero__0), .clk(ENABLE));  // open: en, clr
  Register #(.width(1), .trigger("high")) register_2 (.D(C), .Q(_1), .clk(ENABLE));  // open: en, clr
  Register #(.width(1), .trigger("high")) register_3 (.D(B), .Q(_2), .clk(ENABLE));  // open: en, clr
  Register #(.width(1), .trigger("high")) register_4 (.D(A), .Q(Ultimo__3), .clk(ENABLE));  // open: en, clr

  // Notes on the sheet:
  //   Registro de desplazamiento
endmodule

module Teclado (
  input  ON_OFF,
  input  Carry_in,
  input  Shifter__in,
  input  ENABLE,
  input  CLEAR
);

  wire and_1_out, and_2_out, clock_1_out, keyboard_1_avail, not_3_out, not_4_out, not_5_out, not_6_out,
       not_7_out, not_8_out, not_9_out, not_10_out, registro_de_desplazamiento_1__1,
       registro_de_desplazamiento_1__2, registro_de_desplazamiento_1_primero__0,
       registro_de_desplazamiento_1_ultimo__3, registro_de_desplazamiento_2__1,
       registro_de_desplazamiento_2__2, registro_de_desplazamiento_2_primero__0,
       registro_de_desplazamiento_2_ultimo__3, t_ff_1_q;
  wire [1:0] not_1_out, register_1_q;
  wire [3:0] demultiplexer_1_out0, demultiplexer_1_out1, n4bit_alu_1_d_c, shift_register_1_q3;
  wire [5:0] bit_extender_1_out;
  wire [6:0] bit_extender_2_out, keyboard_1_data;

  Clock clock_1 (.out(clock_1_out));
  Keyboard keyboard_1 (.clk(clock_1_out), .re(ENABLE), .clr(CLEAR), .avail(keyboard_1_avail), .data(keyboard_1_data));
  not not_1 (not_1_out[0], keyboard_1_data[2]);
  not not_2 (not_1_out[1], keyboard_1_data[1]);
  Register #(.width(2), .trigger("high")) register_1 (
    .D(not_1_out), .Q(register_1_q), .clk(and_1_out));  // open: en, clr
  and and_1 (and_1_out, keyboard_1_data[5], keyboard_1_data[3]);
  not not_3 (not_3_out, keyboard_1_avail);
  T_Flip_Flop t_ff_1 (.clk(and_1_out), .T(and_1_out), .Q(t_ff_1_q), .reset(CLEAR), .en(and_1_out));  // open: Qn, preset
  not not_4 (not_4_out, not_5_out);
  not not_5 (not_5_out, not_3_out);
  not not_6 (not_6_out, not_4_out);
  and and_2 (and_2_out, clock_1_out, keyboard_1_avail, not_7_out);
  not not_7 (not_7_out, and_1_out);
  not not_8 (not_8_out, not_6_out);
  not not_9 (not_9_out, not_8_out);
  TTY #(.trigger("falling")) tty_1 (.data(bit_extender_2_out), .clk(not_9_out), .we(ENABLE), .clr(CLEAR));
  // Probe on demultiplexer_1_out0
  Demultiplexer #(.width(4), .enable("false")) demultiplexer_1 (
    .out0(demultiplexer_1_out0), .out1(demultiplexer_1_out1), .in(shift_register_1_q3), .sel(t_ff_1_q));
  Shift_Register #(.length(4)) shift_register_1 (
    .shift(1'b1), .in(keyboard_1_data[0]), .clk(and_2_out), .q0(shift_register_1_q3[3]),
    .q1(shift_register_1_q3[2]), .q2(shift_register_1_q3[1]), .q3(shift_register_1_q3[0]));  // open: out, load, clr, d0, d1, d2, d3
  // Probe on shift_register_1_q3
  registro_de_desplazamiento registro_de_desplazamiento_1 (
    .D(demultiplexer_1_out0[0]), .C(demultiplexer_1_out0[1]), .B(demultiplexer_1_out0[2]),
    .A(demultiplexer_1_out0[3]), .ENABLE(not_10_out), .Primero__0(registro_de_desplazamiento_1_primero__0),
    ._1(registro_de_desplazamiento_1__1), ._2(registro_de_desplazamiento_1__2),
    .Ultimo__3(registro_de_desplazamiento_1_ultimo__3));
  not not_10 (not_10_out, t_ff_1_q);
  registro_de_desplazamiento registro_de_desplazamiento_2 (
    .D(demultiplexer_1_out1[0]), .C(demultiplexer_1_out1[1]), .B(demultiplexer_1_out1[2]),
    .A(demultiplexer_1_out1[3]), .ENABLE(t_ff_1_q), .Primero__0(registro_de_desplazamiento_2_primero__0),
    ._1(registro_de_desplazamiento_2__1), ._2(registro_de_desplazamiento_2__2),
    .Ultimo__3(registro_de_desplazamiento_2_ultimo__3));
  // Probe on bit_extender_2_out
  _4Bit_ALU u_4bit_alu_1 (
    .A_A(registro_de_desplazamiento_1_primero__0), .B_A(registro_de_desplazamiento_1__1),
    .C_A(registro_de_desplazamiento_1__2), .D_A(registro_de_desplazamiento_1_ultimo__3),
    .A_B(registro_de_desplazamiento_2_primero__0), .B_B(registro_de_desplazamiento_2__1),
    .C_B(registro_de_desplazamiento_2__2), .D_B(registro_de_desplazamiento_2_ultimo__3),
    .A_MUX(register_1_q[0]), .B_MUX(register_1_q[1]), .CARRY_IN(Carry_in), .Shifter_In(Shifter__in),
    .CLOCK(ON_OFF), .ON_OFF(clock_1_out), ._5__Vcc(1'b1), ._12__GND(1'b0), .D_C(n4bit_alu_1_d_c[0]),
    .C_C(n4bit_alu_1_d_c[1]), .B_C(n4bit_alu_1_d_c[2]), .A_C(n4bit_alu_1_d_c[3]));  // open: OVERFLOW, CARRY_OUT, Shifter_Out
  assign bit_extender_1_out = {{2{1'b1}}, n4bit_alu_1_d_c};  // Bit_Extender bit_extender_1
  assign bit_extender_2_out = {{1{1'b0}}, bit_extender_1_out};  // Bit_Extender bit_extender_2

  // Notes on the sheet:
  //   Se sugiere ponerlo a 1Hz
  //   La pantalla imprime numeros del 0 al 9,
  //   apartir de ahí imprime los siguientes caracteres ascii
  //   https://ascii.cl/es/
  //   A_Mux
  //   B_Mux
  //   Hay que darle al enable cuando se termine de escribir, o en su defecto, asegurarse de que no se quede vacio antes de terminar de escribir
  //   Se sugiere ON/OFF=1, Carry e Shifter in=0
  //   Clear es necesario cada vez que se quiera escribir otra operacion
  //   Enable
endmodule
