// Logisim project EjercicioLogisimGFS.circ as structural Verilog: 2 circuits, main circuit main
module main (
  input  A,
  input  B,
  input  C
);

  wire and_1_out, clock_1_out, leerescribir_1_d, leerescribir_1_s;
  wire [4:0] adder_1_out, MAR_q;
  wire [7:0] MBR_q, ram_1_data, transistor_1_out;

  LeerEscribir leerescribir_1 (.a(A), .b(B), .c(C), .s(leerescribir_1_s), .d(leerescribir_1_d));
  and and_1 (and_1_out, C, leerescribir_1_d);
  Adder #(.width(5)) adder_1 (.a(MAR_q), .b({5{1'b0}}), .out(adder_1_out), .cin(and_1_out));  // open: cout
  // Probe on MAR_q
  Register #(.width(5)) MAR (.D(adder_1_out), .Q(MAR_q), .clk(clock_1_out));  // open: en, clr
  RAM #(.addrWidth(5)) ram_1 (
    .addr(MAR_q), .data(ram_1_data), .sel(leerescribir_1_d), .clk(clock_1_out), .ld(leerescribir_1_s));  // open: clr
  Clock clock_1 (.out(clock_1_out));
  Transistor #(.gate("br"), .width(8)) transistor_1 (.in(MBR_q), .out(transistor_1_out), .gate(leerescribir_1_s));
  Register MBR (.D(ram_1_data), .Q(MBR_q), .clk(clock_1_out));  // open: en, clr
  assign ram_1_data = transistor_1_out;  // Buffer buffer_1, 8 bits wide

  // Notes on the sheet:
  //   1 lee, 0 escribe
  //   2^5=32 posiciones
endmodule

module LeerEscribir (
  input  a,
  input  b,
  input  c,
  output s,
  output d
);

  wire and_2_out, and_3_out, not_1_out, not_2_out, not_3_out, not_4_out, not_5_out, not_6_out;

  and and_1 (s, a, not_1_out, not_2_out);
  not not_1 (not_1_out, b);
  not not_2 (not_2_out, c);
  not not_3 (not_3_out, a);
  and and_2 (and_2_out, not_3_out, b, not_4_out);
  not not_4 (not_4_out, c);
  not not_5 (not_5_out, a);
  and and_3 (and_3_out, not_5_out, not_6_out, c);
  not not_6 (not_6_out, b);
  or or_1 (d, s, and_2_out, and_3_out);

  // Notes on the sheet:
  //   Botones
  //   Salida al out (1 lee, 0 escribe)
  //   Salida al sel (si es 0 deshabilita el componente)
endmodule
